# Fritzing sketch DALOY AIR (saved by Fritzing 0.9.3b)
breadboards: 1

parts:
  BAT1 = Battery Holders [package=lipo-1100mAh]  # not connected
  R1 = Resistor [tolerance=±5% resistance=220 package="2010 [SMD]"]
  DHT1 = DHT22 Humidity and Temperature Sensor
  Part2 = Adafruit BMP180
  Part3 = Arduino Nano (Rev3.0)
  Part6 = NRF24L01+ Breakout Board
  U1 = Voltage Regulator -- 3.3 V -- LM1117

nets:
  N1: R1.Pin_0, DHT1.DATA, Part3.D2
  VDD: R1.Pin_1, DHT1.VDD, Part2.+3V3, U1.IN
  GND: DHT1.GND, Part2.GND, Part6.GND, U1.GND
  N2: Part2.SCL, Part3.A5
  N3: Part2.SDA, Part3.A4
  N4: Part3.D8, Part6.CS
  N5: Part3.D9, Part6.CE
  N6: Part3.D11/MOSI, Part6.MOSI
  N7: Part3.D12/MISO, Part6.MISO
  N8: Part3.D13/SCK, Part6.SCK
  N9: Part6.VCC, U1.OUT

custom parts:
  Adafruit BMP180: This precision sensor from Bosch is the best low-cost sensing solution for measuring barometric pressure and temperature. Because pressure changes with altitude you can also use it as an altimeter! The sensor is soldered onto a PCB with a 3.3V regulator, I2C level shifter and pull-up resistors on the I2C pins. The BMP180 is the next-generation of sensors from Bosch, and replaces the BMP085.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
  Voltage Regulator -- 3.3 V -- LM1117: LM1117-3.3 Voltage regulator, 3.3 V output. Note that the pinout order is not the same as LM7805 or LM7833.
